// Logisim project seq_circuit.circ as structural Verilog: 1 circuit, main circuit main
module main (
  input  x,
  input  y,
  input  in_3,
  output S,
  output C
);

  wire and_1_out, and_2_out, clock_1_out, xor_1_out;

  Clock clock_1 (.out(clock_1_out));
  xor xor_1 (xor_1_out, x, y);
  D_Flip_Flop d_ff_1 (.clk(clock_1_out), .D(C), .Q(in_3));  // open: Qn, preset, en, reset
  and and_1 (and_1_out, in_3, xor_1_out);
  and and_2 (and_2_out, x, y);
  xor xor_2 (S, xor_1_out, in_3);
  or or_1 (C, and_1_out, and_2_out);

  // Notes on the sheet:
  //   Q
  //   clock
endmodule
